# Fritzing sketch primitiv-controller (saved by Fritzing 0.9.3b)
breadboards: 1

parts:
  Part1 = Arduino Uno (Rev3)
  AMPHENOL_-_ACJS-MHDR_-_JACK_6_35MM1 = AMPHENOL - ACJS-MHDR [package=ACJS-MHDR]
  Pedal = smd LED [color="Orange (620nm)" package="1206 [SMD]"]
  R1 = Resistor [tolerance=±5% resistance=220 package="0603 [SMD]"]
  LED2 = smd LED [color="Green (570nm)" package="1206 [SMD]"]
  LED3 = smd LED [color="Green (570nm)" package="1206 [SMD]"]
  LED4 = smd LED [color="Green (570nm)" package="1206 [SMD]"]
  LED5 = smd LED [color="Green (570nm)" package="1206 [SMD]"]
  R2 = Resistor [tolerance=±5% resistance=220 package="0603 [SMD]"]
  R3 = Resistor [tolerance=±5% resistance=220 package="0603 [SMD]"]
  R4 = Resistor [tolerance=±5% resistance=220 package="0603 [SMD]"]
  R5 = Resistor [tolerance=±5% resistance=220 package="0603 [SMD]"]
  S1 = SWITCH-MOMENTARY-2 [package=tactile-pth]
  S2 = SWITCH-MOMENTARY-2 [package=tactile-pth]
  S3 = SWITCH-MOMENTARY-2 [package=tactile-pth]
  S4 = SWITCH-MOMENTARY-2 [package=tactile-pth]
  PEDAL = POT [package=alps_pot]

nets:
  N1: Part1.A0, AMPHENOL_-_ACJS-MHDR_-_JACK_6_35MM1.Ring_(5)
  N2: Part1.D8, R4.Pin_0
  N3: Part1.D9_PWM, R5.Pin_0
  N4: Part1.D10_PWM/SS, S1.1
  N5: Part1.D11_PWM/MOSI, S2.1
  N6: Part1.D12/MISO, S3.1
  N7: Part1.D13/SCK, S4.1
  N8: Part1.GND, AMPHENOL_-_ACJS-MHDR_-_JACK_6_35MM1.Sleeve_(4), Pedal.cathode, LED2.cathode, LED3.cathode, LED4.cathode, LED5.cathode, S1.2, S2.2, S3.2, S4.2
  N9: Part1.D2, AMPHENOL_-_ACJS-MHDR_-_JACK_6_35MM1.Sleeve_(1), PEDAL.E
  N10: Part1.D4, R2.Pin_0
  N11: Part1.D6_PWM, R1.Pin_0
  N12: Part1.D7, R3.Pin_0
  N13: Part1.5V, AMPHENOL_-_ACJS-MHDR_-_JACK_6_35MM1.Tip_(6)
  N14: AMPHENOL_-_ACJS-MHDR_-_JACK_6_35MM1.Ring_(2), PEDAL.S
  N15: AMPHENOL_-_ACJS-MHDR_-_JACK_6_35MM1.Tip_(3), PEDAL.A
  N16: Pedal.anode, R1.Pin_1
  N17: LED2.anode, R2.Pin_1
  N18: LED3.anode, R3.Pin_1
  N19: LED4.anode, R4.Pin_1
  N20: LED5.anode, R5.Pin_1

notes:
  shielded wire
  Primitive midi controller
  jack detection
